# Fritzing sketch FritzingWithButtons (saved by Fritzing 0.9.3b)
breadboards: 1

parts:
  Part1 = Arduino Leonardo (Rev3b)
  S1 = Pushbutton [package="[SMD]"]
  S2 = Pushbutton [package="[SMD]"]
  S3 = Pushbutton [package="[SMD]"]
  S4 = Pushbutton [package="[SMD]"]
  R1 = Resistor [tolerance=±5% resistance=15k package="1206 [SMD]"]
  R2 = Resistor [tolerance=±5% resistance=15k package="1206 [SMD]"]
  R3 = Resistor [tolerance=±5% resistance=15k package="1206 [SMD]"]
  R4 = Resistor [tolerance=±5% resistance=15k package="1206 [SMD]"]

nets:
  N1: Part1.D2/SDA, Part1.5V, Part1.SDA, S1.Pin_1, S1.Pin_2, S2.Pin_1, S2.Pin_2, S3.Pin_1, S3.Pin_2, S4.Pin_1, S4.Pin_2
  N2: Part1.D7, S4.Pin_3, S4.Pin_4, R3.Pin_1
  N3: Part1.GND, R1.Pin_0, R2.Pin_0, R3.Pin_0, R4.Pin_0
  N4: Part1.D8/A8, S2.Pin_3, S2.Pin_4, R2.Pin_1
  N5: Part1.D12/A11, S1.Pin_3, S1.Pin_4, R1.Pin_1
  N6: S3.Pin_3, S3.Pin_4, R4.Pin_1
